// Digital circuit Adder_1bit.dig as structural Verilog
module Adder_1bit (
  input  A,
  input  B,
  input  CarryIN,
  output S,
  output CarryOUT
);

  wire and_1_out, and_2_out, xor_1_out;

  xor xor_1 (xor_1_out, A, B);
  xor xor_2 (S, xor_1_out, CarryIN);
  and and_1 (and_1_out, CarryIN, xor_1_out);
  and and_2 (and_2_out, A, B);
  or or_1 (CarryOUT, and_1_out, and_2_out);
endmodule
