// Digital circuit Adder_8bits.dig as structural Verilog
module Adder_8bits (
  input  [7:0] A,
  input  [7:0] B,
  input  CarryIN,
  output [7:0] S,
  output CarryOUT
);

  wire adder_1bit_1_carryout, adder_1bit_2_carryout, adder_1bit_3_carryout, adder_1bit_4_carryout,
       adder_1bit_5_carryout, adder_1bit_6_carryout, adder_1bit_7_carryout;

  Adder_1bit adder_1bit_1 (.A(A[0]), .B(B[0]), .CarryIN(CarryIN), .S(S[0]), .CarryOUT(adder_1bit_1_carryout));
  Adder_1bit adder_1bit_2 (
    .A(A[1]), .B(B[1]), .CarryIN(adder_1bit_1_carryout), .S(S[1]), .CarryOUT(adder_1bit_2_carryout));
  Adder_1bit adder_1bit_3 (
    .A(A[2]), .B(B[2]), .CarryIN(adder_1bit_2_carryout), .S(S[2]), .CarryOUT(adder_1bit_3_carryout));
  Adder_1bit adder_1bit_4 (
    .A(A[3]), .B(B[3]), .CarryIN(adder_1bit_3_carryout), .S(S[3]), .CarryOUT(adder_1bit_4_carryout));
  Adder_1bit adder_1bit_5 (
    .A(A[4]), .B(B[4]), .CarryIN(adder_1bit_4_carryout), .S(S[4]), .CarryOUT(adder_1bit_5_carryout));
  Adder_1bit adder_1bit_6 (
    .A(A[5]), .B(B[5]), .CarryIN(adder_1bit_5_carryout), .S(S[5]), .CarryOUT(adder_1bit_6_carryout));
  Adder_1bit adder_1bit_7 (
    .A(A[6]), .B(B[6]), .CarryIN(adder_1bit_6_carryout), .S(S[6]), .CarryOUT(adder_1bit_7_carryout));
  Adder_1bit adder_1bit_8 (.A(A[7]), .B(B[7]), .CarryIN(adder_1bit_7_carryout), .S(S[7]), .CarryOUT(CarryOUT));

  // Other names for the same wires on the sheet: A1 = A[0]; A2 = A[1]; A3 = A[2]; A4 = A[3]; A5 = A[4]; A6 = A[5];
  //   A7 = A[6]; A8 = A[7]; B1 = B[0]; B2 = B[1]; B3 = B[2]; B4 = B[3]; B5 = B[4]; B6 = B[5]; B7 = B[6]; B8 = B[7]
endmodule
