// Digital circuit Multiplier_4Bit.dig as structural Verilog
module Multiplier_4Bit (
  input  [3:0] A,
  input  [3:0] B,
  output [7:0] RESULT
);

  wire [3:0] and_1_out, and_2_out;
  wire [3:1] and_3_out_2, and_4_out_2, undriven, undriven_2, undriven_3;
  wire [4:4] and_4_out;
  wire [5:5] and_3_out;
  wire [7:0] adder_8bits_1_s, adder_8bits_2_s;

  assign and_1_out = A & {undriven_3, B[0]};  // And and_1, 4 bits wide
  assign and_2_out = A & {undriven, B[1]};  // And and_2, 4 bits wide
  assign {and_3_out_2, and_3_out[5]} = A & {undriven_2, B[3]};  // And and_3, 4 bits wide
  assign {and_4_out_2, and_4_out[4]} = A & {undriven_2, B[3]};  // And and_4, 4 bits wide
  Adder_8bits adder_8bits_1 (
    .A({{4{and_1_out[0]}}, 4'b0000}), .B({1'b0, {4{and_2_out[0]}}, 3'b000}), .CarryIN(1'b0),
    .S(adder_8bits_1_s));  // open: CarryOUT
  Adder_8bits adder_8bits_2 (
    .A(adder_8bits_1_s), .B({2'b00, {4{and_3_out[5]}}, 2'b00}), .CarryIN(1'b0), .S(adder_8bits_2_s));  // open: CarryOUT
  Adder_8bits adder_8bits_3 (
    .A(adder_8bits_2_s), .B({3'b000, {4{and_4_out[4]}}, 1'b0}), .CarryIN(1'b0), .S(RESULT));  // open: CarryOUT
  // Pins of 1 and 4 bits meet at {undriven_3, B[0]}
  // Pins of 1 and 4 bits meet at {undriven, B[1]}
  // Pins of 1 and 4 bits meet at {undriven_2, B[3]}
  // Pins of 1 and 4 bits meet at and_2_out
  // Pins of 1 and 4 bits meet at and_1_out
  // Pins of 1 and 4 bits meet at {and_4_out_2, and_4_out[4]}
  // Pins of 1 and 4 bits meet at {and_3_out_2, and_3_out[5]}

  assign B[2] = B[3];
endmodule
