// Digital circuit Soma_Sub.dig as structural Verilog
module Soma_Sub (
  input  [7:0] A,
  input  [7:0] B,
  input  SUB,
  output [7:0] RESULT,
  output CarryOUT
);

  wire [7:0] multiplexer_1_out, not_1_out;

  assign not_1_out = ~B;  // Not not_1, 8 bits wide
  Multiplexer #(.Bits(8)) multiplexer_1 (.sel(SUB), .in_0(B), .in_1(not_1_out), .out(multiplexer_1_out));
  Adder_8bits adder_8bits_1 (.A(A), .B(multiplexer_1_out), .CarryIN(SUB), .S(RESULT), .CarryOUT(CarryOUT));
endmodule
