// Digital circuit uma_coisa_um_pouco_mais_estranha_soma_subtrai_incrementa_e_decrementa_quase_uma_alu_mas_falta_multiplicacao_____seguimos.dig as structural Verilog
module uma_coisa_um_pouco_mais_estranha_soma_subtrai_incrementa_e_decrementa_quase_uma_alu_mas_falta_multiplicacao_____seguimos (
  input  [7:0] A,
  input  [7:0] B,
  input  [1:0] OpCode,
  output [7:0] RESULT
);

  wire multiplexer_2_out;
  wire [7:0] multiplexer_1_out;

  Multiplexer #(.Bits(8), .Selector_Bits(2)) multiplexer_1 (
    .sel(OpCode), .in_0(B), .in_1(B), .in_2(8'h1), .in_3(8'h1), .out(multiplexer_1_out));
  Multiplexer #(.Selector_Bits(2)) multiplexer_2 (
    .sel(OpCode), .in_0(1'b0), .in_1(1'b1), .in_2(1'b0), .in_3(1'b1), .out(multiplexer_2_out));
  Soma_Sub soma_sub_1 (.A(A), .B(multiplexer_1_out), .SUB(multiplexer_2_out), .RESULT(RESULT));  // open: CarryOUT
endmodule
